# Fritzing sketch VolumeKnob (saved by Fritzing 0.9.3b)

parts:
  Raspberry_Pi_Zero1 = Raspberry Pi Zero
  ENCODER1 = Rotary Encoder with Knob
  Part2 = VEML6070 [part_number=VEML6070]

nets:
  N1: Raspberry_Pi_Zero1.GPIO2, Part2.SDA
  N2: Raspberry_Pi_Zero1.GPIO3, Part2.SCL
  N3: Raspberry_Pi_Zero1.3V3, ENCODER1.no_name_yet#5
  N4: Raspberry_Pi_Zero1.GPIO25, ENCODER1.no_name_yet#3
  GND: Raspberry_Pi_Zero1.GND, ENCODER1.no_name_yet#2, Part2.GND
  N5: Raspberry_Pi_Zero1.GPIO24, ENCODER1.no_name_yet#1
  N6: Raspberry_Pi_Zero1.GPIO23, ENCODER1.no_name_yet#4
  5V: Raspberry_Pi_Zero1.5V, Part2.VDD

custom parts:
  Rotary Encoder with Knob: Rotary Encoder with 1/4" Shaft and Knob
  VEML6070: This little sensor is a great way to add UV light sensing to any microcontroller project. The VEML6070 from Vishay has a true UV A light sensor and an I2C-controlled ADC that will take readings and integrate them for you over ~60ms to 500ms.
